// Logisim project 4_REG.circ as structural Verilog: 4 circuits, main circuit main
module main (
  input  D0,
  input  D1,
  input  D2,
  input  D3,
  input  D4,
  input  D5,
  input  D6,
  input  D7,
  input  D8,
  input  D9,
  input  D10,
  input  D11,
  input  D12,
  input  D13,
  input  D14,
  input  D15,
  input  T0,
  input  T1,
  input  T2,
  input  T3,
  input  T4
);

  wire arcontrol_1_bus, arcontrol_1_inc, arcontrol_1_load, pccontrol_1_bus, pccontrol_1_inc, pccontrol_1_load;
  wire [3:0] AR_output, controlled_buffer_1_out, PC_output;

  ARCONTROL arcontrol_1 (
    .D4(D4), .D5(D5), .T0(T0), .T2(T2), .T3(T3), .T4(T4), .LOAD(arcontrol_1_load), .INC(arcontrol_1_inc),
    .BUS(arcontrol_1_bus));
  PCControl pccontrol_1 (
    .D4(D4), .D5(D5), .D6(D6), .T0(T0), .T1(T1), .T3(T3), .T4(T4), .BUS(pccontrol_1_bus),
    .INC(pccontrol_1_inc), .LOAD(pccontrol_1_load));
  _4_REG AR (
    .INPUT(controlled_buffer_1_out), .LD(arcontrol_1_load), .INC(arcontrol_1_inc), .OUTPUT(AR_output));  // open: CLK, CLR
  _4_REG PC (
    .INPUT(controlled_buffer_1_out), .LD(pccontrol_1_load), .INC(pccontrol_1_inc), .OUTPUT(PC_output));  // open: CLK, CLR
  assign controlled_buffer_1_out = arcontrol_1_bus ? AR_output : 4'bz;  // Controlled_Buffer controlled_buffer_1
  assign controlled_buffer_1_out = pccontrol_1_bus ? PC_output : 4'bz;  // Controlled_Buffer controlled_buffer_2
endmodule

// 4REG
module _4_REG (
  input  INC,
  input  LD,
  input  [3:0] INPUT,
  input  CLK,
  input  CLR,
  output [3:0] OUTPUT
);

  wire and_1_out, and_2_out, and_3_out, and_4_out, and_5_out, and_6_out, and_7_out, and_8_out, and_9_out,
       and_10_out, and_11_out, and_12_out, not_1_out, not_2_out, not_3_out, not_4_out, not_5_out, not_6_out,
       or_1_out, or_2_out, or_3_out, or_4_out, or_5_out, or_6_out, or_7_out, or_8_out;

  not not_1 (not_1_out, LD);
  not not_2 (not_2_out, not_1_out);
  not not_3 (not_3_out, INPUT[0]);
  not not_4 (not_4_out, INPUT[1]);
  not not_5 (not_5_out, INPUT[2]);
  not not_6 (not_6_out, INPUT[3]);
  and and_1 (and_1_out, INC, not_1_out);
  and and_2 (and_2_out, not_2_out, INPUT[0]);
  and and_3 (and_3_out, not_2_out, not_3_out);
  and and_4 (and_4_out, not_2_out, INPUT[1]);
  and and_5 (and_5_out, not_2_out, not_4_out);
  and and_6 (and_6_out, not_2_out, INPUT[2]);
  and and_7 (and_7_out, not_2_out, not_5_out);
  and and_8 (and_8_out, not_2_out, INPUT[3]);
  and and_9 (and_9_out, not_2_out, not_6_out);
  and and_10 (and_10_out, and_1_out, OUTPUT[0]);
  and and_11 (and_11_out, and_1_out, OUTPUT[0], OUTPUT[1]);
  and and_12 (and_12_out, and_1_out, OUTPUT[0], OUTPUT[1], OUTPUT[2]);
  or or_1 (or_1_out, and_2_out, and_1_out);
  or or_2 (or_2_out, and_3_out, and_1_out);
  or or_3 (or_3_out, and_4_out, and_10_out);
  or or_4 (or_4_out, and_10_out, and_5_out);
  or or_5 (or_5_out, and_6_out, and_11_out);
  or or_6 (or_6_out, and_11_out, and_7_out);
  or or_7 (or_7_out, and_8_out, and_12_out);
  or or_8 (or_8_out, and_12_out, and_9_out);
  J_K_Flip_Flop j_k_ff_1 (.J(or_1_out), .clk(CLK), .K(or_2_out), .Q(OUTPUT[0]), .reset(CLR));  // open: Qn, preset, en
  J_K_Flip_Flop j_k_ff_2 (.J(or_3_out), .clk(CLK), .K(or_4_out), .Q(OUTPUT[1]), .reset(CLR));  // open: Qn, preset, en
  J_K_Flip_Flop j_k_ff_3 (.J(or_5_out), .clk(CLK), .K(or_6_out), .Q(OUTPUT[2]), .reset(CLR));  // open: Qn, preset, en
  J_K_Flip_Flop j_k_ff_4 (.J(or_7_out), .clk(CLK), .K(or_8_out), .Q(OUTPUT[3]), .reset(CLR));  // open: Qn, preset, en
endmodule

// bcontrl
module PCControl (
  input  D4,
  input  D5,
  input  D6,
  input  T0,
  input  T1,
  input  T3,
  input  T4,
  output BUS,
  output INC,
  output LOAD
);

  wire and_1_out, and_2_out, and_3_out, and_4_out;

  and and_1 (and_1_out, D5, T3);
  and and_2 (and_2_out, D4, T3);
  and and_3 (and_3_out, D6, T3);
  and and_4 (and_4_out, D5, T4);
  or or_1 (BUS, T0, and_1_out);
  or or_2 (LOAD, and_2_out, and_3_out, and_4_out);

  assign INC = T1;
endmodule

module ARCONTROL (
  input  D4,
  input  D5,
  input  T0,
  input  T2,
  input  T3,
  input  T4,
  output LOAD,
  output INC,
  output BUS
);

  wire and_1_out, and_2_out;

  and and_1 (and_1_out, D5, T4);
  and and_2 (and_2_out, D4, T3);
  or or_1 (LOAD, T0, T2);
  and and_3 (INC, T3, D5);
  or or_2 (BUS, and_1_out, and_2_out);
endmodule
