// Logisim project bus_control_4bit_register.circ as structural Verilog: 3 circuits, main circuit main
module main (
  input  C1,
  input  C2
);

  wire asd_1_q1, asd_1_q2, asd_1_q3, clock_1_out;
  wire [3:0] controlled_buffer_1_out, R1_output, R2_output, R3_output;

  Clock clock_1 (.out(clock_1_out));
  asd asd_1 (.C1(C1), .C2(C2), .Q1(asd_1_q1), .Q2(asd_1_q2), .Q3(asd_1_q3));
  _4_REG R1 (.INPUT(controlled_buffer_1_out), .CLK(clock_1_out), .LD(asd_1_q1), .OUTPUT(R1_output));  // open: INC, CLR
  _4_REG R2 (.INPUT(controlled_buffer_1_out), .CLK(clock_1_out), .LD(asd_1_q2), .OUTPUT(R2_output));  // open: INC, CLR
  _4_REG R3 (.INPUT(controlled_buffer_1_out), .CLK(clock_1_out), .LD(asd_1_q3), .OUTPUT(R3_output));  // open: INC, CLR
  // Probe on R1_output
  // Probe on R2_output
  // Probe on R3_output
  assign controlled_buffer_1_out = asd_1_q3 ? R1_output : 4'bz;  // Controlled_Buffer controlled_buffer_1
  assign controlled_buffer_1_out = asd_1_q1 ? R2_output : 4'bz;  // Controlled_Buffer controlled_buffer_2
  assign controlled_buffer_1_out = asd_1_q2 ? R3_output : 4'bz;  // Controlled_Buffer controlled_buffer_3
endmodule

// reg.
module _4_REG (
  input  INC,
  input  LD,
  input  [3:0] INPUT,
  input  CLK,
  input  CLR,
  output [3:0] OUTPUT
);

  wire and_1_out, and_2_out, and_3_out, and_4_out, and_5_out, and_6_out, and_7_out, and_8_out, and_9_out,
       and_10_out, and_11_out, and_12_out, not_1_out, not_2_out, not_3_out, not_4_out, not_5_out, not_6_out,
       or_1_out, or_2_out, or_3_out, or_4_out, or_5_out, or_6_out, or_7_out, or_8_out;

  not not_1 (not_1_out, not_2_out);
  not not_2 (not_2_out, LD);
  not not_3 (not_3_out, INPUT[0]);
  not not_4 (not_4_out, INPUT[1]);
  not not_5 (not_5_out, INPUT[2]);
  not not_6 (not_6_out, INPUT[3]);
  and and_1 (and_1_out, INC, not_2_out);
  and and_2 (and_2_out, not_1_out, INPUT[0]);
  and and_3 (and_3_out, not_1_out, not_3_out);
  and and_4 (and_4_out, not_1_out, INPUT[1]);
  and and_5 (and_5_out, not_1_out, not_4_out);
  and and_6 (and_6_out, not_1_out, INPUT[2]);
  and and_7 (and_7_out, not_1_out, not_5_out);
  and and_8 (and_8_out, not_1_out, INPUT[3]);
  and and_9 (and_9_out, not_1_out, not_6_out);
  and and_10 (and_10_out, and_1_out, OUTPUT[0]);
  and and_11 (and_11_out, and_1_out, OUTPUT[0], OUTPUT[1]);
  and and_12 (and_12_out, and_1_out, OUTPUT[0], OUTPUT[1], OUTPUT[2]);
  or or_1 (or_1_out, and_2_out, and_1_out);
  or or_2 (or_2_out, and_3_out, and_1_out);
  or or_3 (or_3_out, and_4_out, and_10_out);
  or or_4 (or_4_out, and_10_out, and_5_out);
  or or_5 (or_5_out, and_6_out, and_11_out);
  or or_6 (or_6_out, and_11_out, and_7_out);
  or or_7 (or_7_out, and_8_out, and_12_out);
  or or_8 (or_8_out, and_12_out, and_9_out);
  J_K_Flip_Flop j_k_ff_1 (.J(or_1_out), .clk(CLK), .K(or_2_out), .Q(OUTPUT[0]), .reset(CLR));  // open: Qn, preset, en
  J_K_Flip_Flop j_k_ff_2 (.J(or_3_out), .clk(CLK), .K(or_4_out), .Q(OUTPUT[1]), .reset(CLR));  // open: Qn, preset, en
  J_K_Flip_Flop j_k_ff_3 (.J(or_5_out), .clk(CLK), .K(or_6_out), .Q(OUTPUT[2]), .reset(CLR));  // open: Qn, preset, en
  J_K_Flip_Flop j_k_ff_4 (.J(or_7_out), .clk(CLK), .K(or_8_out), .Q(OUTPUT[3]), .reset(CLR));  // open: Qn, preset, en
endmodule

// bcontrl
module asd (
  input  C1,
  input  C2,
  output Q1,
  output Q2,
  output Q3
);

  wire not_1_out, not_2_out, not_3_out, not_4_out;

  not not_1 (not_1_out, C1);
  and and_1 (Q1, not_1_out, not_2_out);
  not not_2 (not_2_out, C2);
  and and_2 (Q2, C2, not_3_out);
  not not_3 (not_3_out, C1);
  not not_4 (not_4_out, C2);
  and and_3 (Q3, not_4_out, C1);
endmodule
