// Logisim project mimarilabproje.circ as structural Verilog: 17 circuits, main circuit main
module main (
  input  [3:0] in_1,
  output out_2
);

  wire and_1_out, clock_1_out, maincontrol_1_acbus, maincontrol_1_acclear, maincontrol_1_acinc,
       maincontrol_1_acload, maincontrol_1_add, maincontrol_1_and, maincontrol_1_arbus,
       \maincontrol_1_ari̇nc , maincontrol_1_arload, maincontrol_1_cil, maincontrol_1_cir, maincontrol_1_cmp,
       maincontrol_1_drload, maincontrol_1_end, maincontrol_1_irbus, maincontrol_1_irload,
       maincontrol_1_ld_dr, maincontrol_1_ld_inpr, maincontrol_1_membus, maincontrol_1_memload,
       maincontrol_1_outload, maincontrol_1_pcbus, maincontrol_1_pcinc, maincontrol_1_pcload, not_1_out;
  wire [3:0] AC_output, AR_output, DR_output, IR_out_6, IR_out_6_2, n4alu_1_output_ac, OUTR_output, PC_output;
  wire [7:0] controlled_buffer_1_out, ram_1_data;

  Clock clock_1 (.out(clock_1_out));
  MainControl maincontrol_1 (
    .IR_4__7(IR_out_6_2), .CLK(and_1_out), .MEMLOAD(maincontrol_1_memload), .MEMBUS(maincontrol_1_membus),
    .ARLOAD(maincontrol_1_arload), .\ARİNC (\maincontrol_1_ari̇nc ), .ARBUS(maincontrol_1_arbus),
    .PCBUS(maincontrol_1_pcbus), .PCINC(maincontrol_1_pcinc), .PCLOAD(maincontrol_1_pcload),
    .DRLOAD(maincontrol_1_drload), .ACLOAD(maincontrol_1_acload), .ACBUS(maincontrol_1_acbus),
    .ACCLEAR(maincontrol_1_acclear), .ACINC(maincontrol_1_acinc), .AND(maincontrol_1_and),
    .ADD(maincontrol_1_add), .LD_DR(maincontrol_1_ld_dr), .CMP(maincontrol_1_cmp), .CIR(maincontrol_1_cir),
    .CIL(maincontrol_1_cil), .LD_INPR(maincontrol_1_ld_inpr), .IRLOAD(maincontrol_1_irload),
    .OUTLOAD(maincontrol_1_outload), .IRBUS(maincontrol_1_irbus), .\end (maincontrol_1_end));
  not not_1 (not_1_out, maincontrol_1_end);
  and and_1 (and_1_out, not_1_out, clock_1_out);
  _4alu u_4alu_1 (
    .ac(AC_output), .dr(DR_output), .\ınpr (in_1), .\and (maincontrol_1_and), .add(maincontrol_1_add),
    .cma(maincontrol_1_cmp), .ld_dr(maincontrol_1_ld_dr), .\ld_ınpr (maincontrol_1_ld_inpr),
    .\cır (maincontrol_1_cir), .\cıl (maincontrol_1_cil), .output_ac(n4alu_1_output_ac), .ELDE(out_2),
    .CLK(and_1_out));  // open: CLR
  RAM #(.addrWidth(4), .bus("separate")) ram_1 (
    .addr(AR_output), .din(controlled_buffer_1_out), .data(ram_1_data), .str(maincontrol_1_memload),
    .clk(and_1_out));  // open: sel, ld, clr
  // Probe on AR_output
  _4_REG AR (
    .INPUT(controlled_buffer_1_out[3:0]), .CLK(and_1_out), .LD(maincontrol_1_arload),
    .INC(\maincontrol_1_ari̇nc ), .OUTPUT(AR_output));  // open: CLR
  // Probe on PC_output
  _4_REG PC (
    .INPUT(controlled_buffer_1_out[3:0]), .CLK(and_1_out), .LD(maincontrol_1_pcload),
    .INC(maincontrol_1_pcinc), .OUTPUT(PC_output));  // open: CLR
  // Probe on DR_output
  _4_REG DR (
    .INPUT(controlled_buffer_1_out[3:0]), .CLK(and_1_out), .LD(maincontrol_1_drload), .OUTPUT(DR_output));  // open: INC, CLR
  // Probe on AC_output
  _4_REG AC (
    .INPUT(n4alu_1_output_ac), .CLK(and_1_out), .LD(maincontrol_1_acload), .INC(maincontrol_1_acinc),
    .CLR(maincontrol_1_acclear), .OUTPUT(AC_output));
  // Probe on {IR_out_6_2, IR_out_6}
  _8_REG IR (
    .in_1(controlled_buffer_1_out), .CLK(and_1_out), .LOAD(maincontrol_1_irload),
    .out_6({IR_out_6_2, IR_out_6}));  // open: INC, CLEAR
  _4_REG OUTR (
    .INPUT(controlled_buffer_1_out[3:0]), .CLK(and_1_out), .LD(maincontrol_1_outload), .OUTPUT(OUTR_output));  // open: INC, CLR
  assign controlled_buffer_1_out = maincontrol_1_membus ? ram_1_data : 8'bz;  // Controlled_Buffer controlled_buffer_1
  assign controlled_buffer_1_out = maincontrol_1_arbus ? {4'b0000, AR_output} : 8'bz;  // Controlled_Buffer controlled_buffer_2
  assign controlled_buffer_1_out = maincontrol_1_pcbus ? {4'b0000, PC_output} : 8'bz;  // Controlled_Buffer controlled_buffer_3
  assign controlled_buffer_1_out = maincontrol_1_acbus ? {4'b0000, AC_output} : 8'bz;  // Controlled_Buffer controlled_buffer_4
  assign controlled_buffer_1_out = maincontrol_1_irbus ? {IR_out_6_2, IR_out_6} : 8'bz;  // Controlled_Buffer controlled_buffer_5
  // Probe on OUTR_output
endmodule

// 4REG
module _4_REG (
  input  INC,
  input  LD,
  input  [3:0] INPUT,
  input  CLK,
  input  CLR,
  output [3:0] OUTPUT
);

  wire and_1_out, and_2_out, and_3_out, and_4_out, and_5_out, and_6_out, and_7_out, and_8_out, and_9_out,
       and_10_out, and_11_out, and_12_out, not_1_out, not_2_out, not_3_out, not_4_out, not_5_out, not_6_out,
       or_1_out, or_2_out, or_3_out, or_4_out, or_5_out, or_6_out, or_7_out, or_8_out;

  not not_1 (not_1_out, LD);
  not not_2 (not_2_out, not_1_out);
  not not_3 (not_3_out, INPUT[0]);
  not not_4 (not_4_out, INPUT[1]);
  not not_5 (not_5_out, INPUT[2]);
  not not_6 (not_6_out, INPUT[3]);
  and and_1 (and_1_out, INC, not_1_out);
  and and_2 (and_2_out, not_2_out, INPUT[0]);
  and and_3 (and_3_out, not_2_out, not_3_out);
  and and_4 (and_4_out, not_2_out, INPUT[1]);
  and and_5 (and_5_out, not_2_out, not_4_out);
  and and_6 (and_6_out, not_2_out, INPUT[2]);
  and and_7 (and_7_out, not_2_out, not_5_out);
  and and_8 (and_8_out, not_2_out, INPUT[3]);
  and and_9 (and_9_out, not_2_out, not_6_out);
  and and_10 (and_10_out, and_1_out, OUTPUT[0]);
  and and_11 (and_11_out, and_1_out, OUTPUT[0], OUTPUT[1]);
  and and_12 (and_12_out, and_1_out, OUTPUT[0], OUTPUT[1], OUTPUT[2]);
  or or_1 (or_1_out, and_2_out, and_1_out);
  or or_2 (or_2_out, and_3_out, and_1_out);
  or or_3 (or_3_out, and_4_out, and_10_out);
  or or_4 (or_4_out, and_10_out, and_5_out);
  or or_5 (or_5_out, and_6_out, and_11_out);
  or or_6 (or_6_out, and_11_out, and_7_out);
  or or_7 (or_7_out, and_8_out, and_12_out);
  or or_8 (or_8_out, and_12_out, and_9_out);
  J_K_Flip_Flop j_k_ff_1 (.J(or_1_out), .clk(CLK), .K(or_2_out), .Q(OUTPUT[0]), .reset(CLR));  // open: Qn, preset, en
  J_K_Flip_Flop j_k_ff_2 (.J(or_3_out), .clk(CLK), .K(or_4_out), .Q(OUTPUT[1]), .reset(CLR));  // open: Qn, preset, en
  J_K_Flip_Flop j_k_ff_3 (.J(or_5_out), .clk(CLK), .K(or_6_out), .Q(OUTPUT[2]), .reset(CLR));  // open: Qn, preset, en
  J_K_Flip_Flop j_k_ff_4 (.J(or_7_out), .clk(CLK), .K(or_8_out), .Q(OUTPUT[3]), .reset(CLR));  // open: Qn, preset, en
endmodule

// PCCNTRL
module PCControl (
  input  D4,
  input  D5,
  input  D6,
  input  T0,
  input  T1,
  input  T3,
  input  T4,
  output BUS,
  output INC,
  output LOAD
);

  wire and_1_out, and_2_out, and_3_out, and_4_out;

  and and_1 (and_1_out, D5, T3);
  and and_2 (and_2_out, D4, T3);
  and and_3 (and_3_out, D6, T3);
  and and_4 (and_4_out, D5, T4);
  or or_1 (BUS, T0, and_1_out);
  or or_2 (LOAD, and_2_out, and_3_out, and_4_out);

  assign INC = T1;
endmodule

// ARCNTRL
module ARCONTROL (
  input  D4,
  input  D5,
  input  T0,
  input  T2,
  input  T3,
  input  T4,
  output LOAD,
  output INC,
  output BUS
);

  wire and_1_out, and_2_out;

  and and_1 (and_1_out, D5, T4);
  and and_2 (and_2_out, D4, T3);
  or or_1 (LOAD, T0, T2);
  and and_3 (INC, T3, D5);
  or or_2 (BUS, and_1_out, and_2_out);
endmodule

// DRCNTRL
module DRCONTROL (
  input  D0,
  input  D1,
  input  D2,
  input  T3,
  output LOAD
);

  wire and_1_out, and_2_out, and_3_out;

  and and_1 (and_1_out, D0, T3);
  and and_2 (and_2_out, T3, D2);
  and and_3 (and_3_out, T3, D1);
  or or_1 (LOAD, and_1_out, and_2_out, and_3_out);
endmodule

// 8REG
module _8_REG (
  input  [7:0] in_1,
  input  CLK,
  input  LOAD,
  input  INC,
  input  CLEAR,
  output [7:0] out_6
);

  _4_REG u_4_reg_1 (.INPUT(in_1[3:0]), .CLK(CLK), .LD(LOAD), .INC(INC), .CLR(CLEAR), .OUTPUT(out_6[3:0]));
  _4_REG u_4_reg_2 (.INPUT(in_1[7:4]), .CLK(CLK), .LD(LOAD), .INC(INC), .CLR(CLEAR), .OUTPUT(out_6[7:4]));
endmodule

// MEMCNTRL
module MEMCONTROL (
  input  D0,
  input  D1,
  input  D2,
  input  D3,
  input  D5,
  input  D6,
  input  T1,
  input  T3,
  output LOAD,
  output BUS
);

  wire and_1_out, and_2_out, and_3_out, and_4_out, and_5_out, and_6_out;

  and and_1 (and_1_out, D3, T3);
  or or_1 (LOAD, and_1_out, and_2_out);
  and and_2 (and_2_out, D5, T3);
  and and_3 (and_3_out, D0, T3);
  and and_4 (and_4_out, D1, T3);
  and and_5 (and_5_out, D2, T3);
  and and_6 (and_6_out, D6, T3);
  or or_2 (BUS, and_3_out, and_4_out, T1, and_5_out, and_6_out);
endmodule

module IRCONTROL (
  input  T1,
  input  T2,
  output LOAD,
  output BUS
);


  assign BUS = T2;
  assign LOAD = T1;
endmodule

// 4BİTALU
module _4alu (
  input  [3:0] ac,
  input  [3:0] dr,
  input  [3:0] \ınpr ,
  input  \and ,
  input  add,
  input  cma,
  input  ld_dr,
  input  \ld_ınpr ,
  input  \cır ,
  input  \cıl ,
  input  CLR,
  input  CLK,
  output [3:0] output_ac,
  output ELDE
);

  wire elde_1_ac_0__ac_i_1, elde_1_ac_0__cin, elde_1_ac_3__ac_i_1, n1alu_1_cout, n1alu_2_cout, n1alu_3_cout,
       n1alu_4_cout;

  _1alu u_1alu_1 (
    .AND(\and ), .ADD(add), .CMA(cma), .LD_DR(ld_dr), .CIR(\ld_ınpr ), .CIR_2(\cır ), .CIR_3(\cıl ),
    .AC_I_1(elde_1_ac_0__ac_i_1), .AC_I_1_2(ac[1]), .INPR(\ınpr [0]), .DR(dr[0]), .AC(ac[0]),
    .CIN_ELDE(elde_1_ac_0__cin), .COUT(n1alu_1_cout), .OUTPUT_AC(output_ac[0]));
  _1alu u_1alu_2 (
    .AND(\and ), .ADD(add), .CMA(cma), .LD_DR(ld_dr), .CIR(\ld_ınpr ), .CIR_2(\cır ), .CIR_3(\cıl ),
    .AC_I_1(ac[0]), .AC_I_1_2(ac[2]), .INPR(\ınpr [1]), .DR(dr[1]), .AC(ac[1]), .CIN_ELDE(n1alu_1_cout),
    .COUT(n1alu_2_cout), .OUTPUT_AC(output_ac[1]));
  _1alu u_1alu_3 (
    .AND(\and ), .ADD(add), .CMA(cma), .LD_DR(ld_dr), .CIR(\ld_ınpr ), .CIR_2(\cır ), .CIR_3(\cıl ),
    .AC_I_1(ac[1]), .AC_I_1_2(ac[3]), .INPR(\ınpr [2]), .DR(dr[2]), .AC(ac[2]), .CIN_ELDE(n1alu_2_cout),
    .COUT(n1alu_3_cout), .OUTPUT_AC(output_ac[2]));
  _1alu u_1alu_4 (
    .AND(\and ), .ADD(add), .CMA(cma), .LD_DR(ld_dr), .CIR(\ld_ınpr ), .CIR_2(\cır ), .CIR_3(\cıl ),
    .AC_I_1(ac[2]), .AC_I_1_2(elde_1_ac_3__ac_i_1), .INPR(\ınpr [3]), .DR(dr[3]), .AC(ac[3]),
    .CIN_ELDE(n1alu_3_cout), .COUT(n1alu_4_cout), .OUTPUT_AC(output_ac[3]));
  ELDE elde_1 (
    .AC_3__cout(n1alu_4_cout), .AC_3__output(output_ac[3]), .AC_0__output(output_ac[0]), .CIL(\cıl ),
    .CIR(\cır ), .ADD(add), .CLK(CLK), .CLR(CLR), .OUTPUT(ELDE), .AC_0__ac_i_1(elde_1_ac_0__ac_i_1),
    .AC_3__ac_i_1(elde_1_ac_3__ac_i_1), .AC_0__cin(elde_1_ac_0__cin));
endmodule

// ALU
module _1alu (
  input  INPR,
  input  DR,
  input  AC,
  input  AND,
  input  CIN_ELDE,
  input  ADD,
  input  CMA,
  input  LD_DR,
  input  CIR,
  input  CIR_2,
  input  CIR_3,
  input  AC_I_1,
  input  AC_I_1_2,
  output COUT,
  output OUTPUT_AC
);

  wire ADD_out, adder_1_out, AND_out, COMP_out, ID_DR_out, LD_INPR_out, not_1_out, SHL_out, SHR_out;

  Adder #(.width(1)) adder_1 (.a(AC), .b(DR), .out(adder_1_out), .cin(CIN_ELDE), .cout(COUT));
  and u_AND (AND_out, AND, AC, DR);
  and u_ADD (ADD_out, ADD, adder_1_out);
  and COMP (COMP_out, CMA, not_1_out);
  not not_1 (not_1_out, AC);
  and ID_DR (ID_DR_out, LD_DR, DR);
  and LD_INPR (LD_INPR_out, CIR, INPR);
  and SHR (SHR_out, CIR_2, AC_I_1_2);
  and SHL (SHL_out, CIR_3, AC_I_1);
  or or_1 (OUTPUT_AC, AND_out, ADD_out, COMP_out, ID_DR_out, LD_INPR_out, SHR_out, SHL_out);
endmodule

module ACCNTRLR (
  input  D0,
  input  D1,
  input  D2,
  input  D3,
  input  D7,
  input  D9,
  input  D10,
  input  D11,
  input  D12,
  input  D13,
  input  D14,
  input  T3,
  input  T4,
  output LOAD,
  output BUS,
  output CLEAR,
  output INC
);

  wire and_1_out, and_2_out, and_3_out, and_4_out, and_5_out, and_6_out, and_7_out, and_8_out, and_9_out;

  and and_1 (and_1_out, T4, D0);
  and and_2 (and_2_out, D1, T4);
  and and_3 (and_3_out, D2, T4);
  and and_4 (and_4_out, D11, T3);
  and and_5 (and_5_out, D12, T3);
  and and_6 (and_6_out, D13, T3);
  and and_7 (and_7_out, T3, D9);
  and and_8 (and_8_out, D3, T3);
  and and_9 (and_9_out, D14, T3);
  and and_10 (CLEAR, D7, T3);
  and and_11 (INC, D10, T3);
  or or_1 (LOAD, and_1_out, and_2_out, and_3_out, and_7_out, and_4_out, and_5_out, and_6_out);
  or or_2 (BUS, and_8_out, and_9_out);
endmodule

// OUTCNTRL
module OUTRCNTRL (
  input  D14,
  input  T3,
  output LOAD
);

  and and_1 (LOAD, T3, D14);
endmodule

// MAINCONTROL
module MainControl (
  input  CLK,
  input  [3:0] IR_4__7,
  output MEMLOAD,
  output MEMBUS,
  output ARLOAD,
  output \ARİNC ,
  output ARBUS,
  output PCBUS,
  output PCINC,
  output PCLOAD,
  output DRLOAD,
  output ACLOAD,
  output ACBUS,
  output ACCLEAR,
  output ACINC,
  output AND,
  output ADD,
  output LD_DR,
  output CMP,
  output CIR,
  output CIL,
  output LD_INPR,
  output IRLOAD,
  output OUTLOAD,
  output IRBUS,
  output \end 
);

  wire decoder_1_out0, decoder_1_out1, decoder_1_out2, decoder_1_out3, decoder_1_out4, decoder_1_out5,
       decoder_1_out6, decoder_1_out7, decoder_1_out8, decoder_1_out9, decoder_1_out10, decoder_1_out11,
       decoder_1_out12, decoder_1_out13, decoder_1_out14, decoder_1_out15, decoder_2_out0, decoder_2_out1,
       decoder_2_out2, decoder_2_out3, decoder_2_out4, sc_clrcntrl_1_sc_0;
  wire [3:0] counter_1_out_3;

  Decoder #(.select(4), .enable("false")) decoder_1 (
    .out0(decoder_1_out0), .out1(decoder_1_out1), .out2(decoder_1_out2), .out3(decoder_1_out3),
    .out4(decoder_1_out4), .out5(decoder_1_out5), .out6(decoder_1_out6), .out7(decoder_1_out7),
    .out8(decoder_1_out8), .out9(decoder_1_out9), .out10(decoder_1_out10), .out11(decoder_1_out11),
    .out12(decoder_1_out12), .out13(decoder_1_out13), .out14(decoder_1_out14), .out15(decoder_1_out15),
    .sel(IR_4__7));
  Decoder #(.select(4), .enable("false")) decoder_2 (
    .out0(decoder_2_out0), .out1(decoder_2_out1), .out2(decoder_2_out2), .out3(decoder_2_out3),
    .out4(decoder_2_out4), .sel(counter_1_out_3));  // open: out5, out6, out7, out8, out9, out10, out11, out12, out13, out14, out15
  and and_1 (\end , decoder_2_out3, decoder_1_out15);
  COUNTER counter_1 (.CLK(CLK), .SC_CLR(sc_clrcntrl_1_sc_0), .out_3(counter_1_out_3));
  MEMCONTROL memcontrol_1 (
    .LOAD(MEMLOAD), .BUS(MEMBUS), .D0(decoder_1_out0), .D1(decoder_1_out1), .D2(decoder_1_out2),
    .D3(decoder_1_out3), .D5(decoder_1_out5), .D6(decoder_1_out6), .T1(decoder_2_out1), .T3(decoder_2_out3));
  ARCONTROL arcontrol_1 (
    .BUS(ARBUS), .INC(\ARİNC ), .D4(decoder_1_out4), .D5(decoder_1_out5), .T0(decoder_2_out0),
    .T2(decoder_2_out2), .T3(decoder_2_out3), .T4(decoder_2_out4), .LOAD(ARLOAD));
  PCControl pccontrol_1 (
    .BUS(PCBUS), .INC(PCINC), .LOAD(PCLOAD), .D4(decoder_1_out4), .D5(decoder_1_out5), .D6(decoder_1_out6),
    .T0(decoder_2_out0), .T1(decoder_2_out1), .T3(decoder_2_out3), .T4(decoder_2_out4));
  DRCONTROL drcontrol_1 (
    .LOAD(DRLOAD), .D0(decoder_1_out0), .D1(decoder_1_out1), .D2(decoder_1_out2), .T3(decoder_2_out3));
  ACCNTRLR accntrlr_1 (
    .LOAD(ACLOAD), .BUS(ACBUS), .CLEAR(ACCLEAR), .INC(ACINC), .D0(decoder_1_out0), .D1(decoder_1_out1),
    .D2(decoder_1_out2), .D3(decoder_1_out3), .D7(decoder_1_out7), .D9(decoder_1_out9),
    .D10(decoder_1_out10), .D11(decoder_1_out11), .D12(decoder_1_out12), .D13(decoder_1_out13),
    .D14(decoder_1_out14), .T3(decoder_2_out3), .T4(decoder_2_out4));
  IRCONTROL ircontrol_1 (.LOAD(IRLOAD), .BUS(IRBUS), .T1(decoder_2_out1), .T2(decoder_2_out2));
  OUTRCNTRL outrcntrl_1 (.D14(decoder_1_out14), .T3(decoder_2_out3), .LOAD(OUTLOAD));
  SC_CLRCNTRL sc_clrcntrl_1 (
    .D0(decoder_1_out0), .D1(decoder_1_out1), .D2(decoder_1_out2), .D3(decoder_1_out3), .D4(decoder_1_out4),
    .D5(decoder_1_out5), .D6(decoder_1_out6), .D7(decoder_1_out7), .D8(decoder_1_out8), .D9(decoder_1_out9),
    .D10(decoder_1_out10), .D11(decoder_1_out11), .D12(decoder_1_out12), .D13(decoder_1_out13),
    .D14(decoder_1_out14), .T3(decoder_2_out3), .T4(decoder_2_out4), .SC_0(sc_clrcntrl_1_sc_0));
  ALUCNTRLR alucntrlr_1 (
    .AND(AND), .ADD(ADD), .LD_DR(LD_DR), .CMP(CMP), .CIR(CIR), .CIL(CIL), .LD_INPR(LD_INPR),
    .D0(decoder_1_out0), .D1(decoder_1_out1), .D2(decoder_1_out2), .D9(decoder_1_out9),
    .D11(decoder_1_out11), .D12(decoder_1_out12), .D13(decoder_1_out13), .T3(decoder_2_out3),
    .T4(decoder_2_out4));
endmodule

module ALUCNTRLR (
  input  D0,
  input  D1,
  input  D2,
  input  D9,
  input  D11,
  input  D12,
  input  D13,
  input  T3,
  input  T4,
  output AND,
  output ADD,
  output LD_DR,
  output CMP,
  output CIR,
  output CIL,
  output LD_INPR
);

  and and_1 (AND, D0, T4);
  and and_2 (ADD, D1, T4);
  and and_3 (LD_DR, D2, T4);
  and and_4 (CMP, D9, T3);
  and and_5 (CIR, D11, T3);
  and and_6 (CIL, D12, T3);
  and and_7 (LD_INPR, D13, T3);
endmodule

module COUNTER (
  input  CLK,
  input  SC_CLR,
  output [3:0] out_3
);

  wire and_1_out, register_1_q;

  Counter #(.width(4), .max('hf)) counter_1 (
    .count(1'b1), .Q(out_3), .clk(CLK), .clr(register_1_q));  // open: load, D, carry
  Register #(.width(1)) register_1 (.D(SC_CLR), .Q(register_1_q), .clk(CLK), .clr(and_1_out));  // open: en
  and and_1 (and_1_out, CLK, SC_CLR);
endmodule

// SC_CLR
module SC_CLRCNTRL (
  input  D0,
  input  D1,
  input  D2,
  input  D3,
  input  D4,
  input  D5,
  input  D6,
  input  D7,
  input  D8,
  input  D9,
  input  D10,
  input  D11,
  input  D12,
  input  D13,
  input  D14,
  input  T3,
  input  T4,
  output SC_0
);

  wire and_1_out, and_2_out, and_3_out, and_4_out, and_5_out, and_6_out, and_7_out, and_8_out, and_9_out,
       and_10_out, and_11_out, and_12_out, and_13_out, and_14_out, and_15_out;

  and and_1 (and_1_out, D0, T4);
  and and_2 (and_2_out, D1, T4);
  and and_3 (and_3_out, D2, T4);
  and and_4 (and_4_out, D3, T3);
  and and_5 (and_5_out, D4, T3);
  and and_6 (and_6_out, D5, T4);
  and and_7 (and_7_out, D6, T3);
  and and_8 (and_8_out, D7, T3);
  and and_9 (and_9_out, D8, T3);
  and and_10 (and_10_out, D9, T3);
  and and_11 (and_11_out, D10, T3);
  and and_12 (and_12_out, D11, T3);
  and and_13 (and_13_out, D12, T3);
  and and_14 (and_14_out, D13, T3);
  and and_15 (and_15_out, D14, T3);
  or or_1 (SC_0, and_1_out, and_2_out, and_3_out, and_4_out, and_5_out, and_6_out, and_7_out, and_8_out, and_9_out, and_10_out, and_11_out, and_12_out, and_13_out, and_14_out, and_15_out);
endmodule

module ELDE (
  input  AC_3__cout,
  input  AC_3__output,
  input  AC_0__output,
  input  CIL,
  input  CIR,
  input  ADD,
  input  CLK,
  input  CLR,
  output OUTPUT,
  output AC_0__ac_i_1,
  output AC_3__ac_i_1,
  output AC_0__cin
);

  wire and_1_out, and_2_out, and_3_out, and_4_out, and_5_out, d_ff_1_q, not_1_out, or_1_out, or_2_out;

  or or_1 (or_1_out, AC_3__cout, AC_3__output, AC_0__output);
  and and_1 (and_1_out, AC_3__cout, ADD);
  and and_2 (and_2_out, AC_0__output, CIR);
  and and_3 (and_3_out, AC_3__output, CIL);
  or or_2 (or_2_out, and_1_out, and_2_out, and_3_out);
  and and_4 (and_4_out, or_2_out, or_1_out);
  and and_5 (and_5_out, or_1_out, not_1_out);
  not not_1 (not_1_out, or_2_out);
  J_K_Flip_Flop j_k_ff_1 (.J(and_4_out), .clk(CLK), .K(and_5_out), .Q(OUTPUT), .reset(CLR));  // open: Qn, preset, en
  D_Flip_Flop d_ff_1 (.clk(CLK), .D(OUTPUT), .Q(d_ff_1_q), .reset(CLR));  // open: Qn, preset, en
  and and_6 (AC_0__ac_i_1, CIL, d_ff_1_q);
  and and_7 (AC_3__ac_i_1, CIR, d_ff_1_q);
  and and_8 (AC_0__cin, ADD, d_ff_1_q);
endmodule
